# Fritzing sketch Sketch 1 Prototype кон_МП (saved by Fritzing 0.9.10b)

parts:
  HC-SR04_Sensor_1 = HC-SR04 Ultrasonic Distance Sensor
  L298N2 = L298N DC motor driver
  M3 = DC Motor [voltage_(max)=6V voltage_(min)=3V]
  M4 = DC Motor [voltage_(max)=6V voltage_(min)=3V]
  Компонент1 = Arduino Nano (Rev3.0)
  J1 = Power Jack [package=power_jack_pth_lock]
  U1 = LM2596 step down module
  Raspberry_Pi_1 = Raspberry Pi 3 [part_number=RPI-3-V1.2]  # not connected
  S2 = Toggle Switch [package=THT]
  X1 = USB Connectors [package=usb-a-s-nosilk]
  C2 = Ceramic Capacitor [capacitance=1µF voltage=35V package="100 mil [THT, multilayer]"]
  C3 = Ceramic Capacitor [capacitance=1µF voltage=35V package="100 mil [THT, multilayer]"]
  C4 = Ceramic Capacitor [capacitance=1µF voltage=35V package="100 mil [THT, multilayer]"]

nets:
  VCC: HC-SR04_Sensor_1.VCC, Компонент1.5V
  N1: HC-SR04_Sensor_1.TRIG, Компонент1.D2
  N2: HC-SR04_Sensor_1.ECHO, Компонент1.D4
  GND: HC-SR04_Sensor_1.GND, L298N2.GND, Компонент1.GND, Компонент1.RESET, J1.GND, J1.GNDBREAK, U1.IN-, U1.OUT-, X1.GND, C4.1
  N3: L298N2.OUT1, M4.pin_2, C3.1
  N4: L298N2.OUT2, M4.pin_1, C3.0
  N5: L298N2.OUT3, M3.pin_2, C2.0
  N6: L298N2.OUT4, M3.pin_1, C2.1
  N7: L298N2.12V, U1.IN+, S2.COM
  N8: L298N2.5V#9, L298N2.ENA
  N9: L298N2.5V#10, L298N2.ENB
  N10: L298N2.IN1, Компонент1.D10, Компонент1.D11/MOSI
  N11: L298N2.IN2, Компонент1.D9
  N12: L298N2.IN3, Компонент1.D6
  N13: L298N2.IN4, Компонент1.D5
  N14: J1.PWR, S2.L1
  N15: U1.OUT+, X1.VBUS

notes:
  Raspberry Pi 3
  подключена к камере OV5647, питается от USB кабеля
  Понижающий DC-DC преобразователь выход 5V, 2A
  2 мотора 12GAN-20
  с керамическими конденсаторами 0.1мкф
  Ультразвуковой датчик HC-SR04
  DC Драйвер для моторов
  L298N2
  PowerJack с кабелем на 12V, подключен к тумблеру
  Arduino Nano(rev.3)
  отладочная плата с
  конденсатором 0.1мкф
  Подключение Arduino к Raspberry Pi по USB порту с использованием протокола UART

custom parts:
  L298N DC motor driver: 2x DC motor driver with 78M05 positive voltage regulator (7..35 V) L298N: max 46 V, 2 A Set 5 V Enable jumper to enable 5 V regultor (needed for the L298N) and +5 V output at screw terminal or supply external +5 V at screw terminal Set ENA and/or ENB to +5 V to enable motor permanently or supply ENA and/or ENB with PWM signal IN1 and IN2 set rotation directory for motor A (OUT1/OUT2) IN2 and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
  LM2596 step down module: LM2596 DC-DC step down power supply module 3 A.
